// Digital circuit 4bit_ALU.dig as structural Verilog
module _4bit_ALU (
  input  [3:0] A,
  input  [3:0] B,
  input  [2:0] Control,
  output [3:0] Output,
  output Zero_Flag
);

  wire [0:0] SLT_slt_flag;
  wire [3:0] ADD_sum, and_1_out, notconnected_1_out, notconnected_2_out, or_1_out, SUB_diff, xor_1_out;

  _4bit_full_adder ADD (.A(A), .B(B), .Ci_1(1'b0), .Sum(ADD_sum));  // open: Overflow
  _4bit_adder_subractor_NEW SUB (.K(1'b1), .A(A), .B(B), .diff(SUB_diff));  // open: C
  assign and_1_out = A & B;  // And and_1, 4 bits wide
  assign or_1_out = A | B;  // Or or_1, 4 bits wide
  assign xor_1_out = A ^ B;  // XOr xor_1, 4 bits wide
  _4bit_SLT SLT (.A(A), .B(B), .SLT_Flag(SLT_slt_flag[0]));
  Multiplexer #(.Selector_Bits(3), .Bits(4)) multiplexer_1 (
    .sel(Control), .in_0(ADD_sum), .in_1(SUB_diff), .in_2(and_1_out), .in_3(or_1_out), .in_4(xor_1_out),
    .in_5({3'b000, SLT_slt_flag[0]}), .in_6(notconnected_1_out), .in_7(notconnected_2_out), .out(Output));
  // NotConnected on notconnected_1_out
  // NotConnected on notconnected_2_out
  nor nor_1 (Zero_Flag, Output[0], Output[1], Output[2], Output[3]);
endmodule
