// Digital circuit 4bit_SLT.dig as structural Verilog
module _4bit_SLT (
  input  [3:0] A,
  input  [3:0] B,
  output SLT_Flag
);

  wire _4bit_adder_subractor_new_1_c;

  _4bit_adder_subractor_NEW _4bit_adder_subractor_new_1 (
    .K(1'b1), .A(A), .B(B), .C(_4bit_adder_subractor_new_1_c));  // open: diff
  not not_1 (SLT_Flag, _4bit_adder_subractor_new_1_c);
endmodule
