// Digital circuit 4bit_adder_subractor_NEW.dig as structural Verilog
module _4bit_adder_subractor_NEW (
  input  K,
  input  [3:0] A,
  input  [3:0] B,
  output C,
  output [3:0] diff
);

  wire _2_0_cout, _2_1_cout, _2_2_cout, xor_1_out, xor_2_out, xor_3_out, xor_4_out;

  xor xor_1 (xor_1_out, B[0], K);
  _1bit_full_adder _2_0 (.A(A[0]), .B(xor_1_out), .Cin(K), .Sum(diff[0]), .Cout(_2_0_cout));
  xor xor_2 (xor_2_out, B[1], K);
  _1bit_full_adder _2_1 (.A(A[1]), .B(xor_2_out), .Cin(_2_0_cout), .Sum(diff[1]), .Cout(_2_1_cout));
  xor xor_3 (xor_3_out, B[2], K);
  _1bit_full_adder _2_2 (.A(A[2]), .B(xor_3_out), .Cin(_2_1_cout), .Sum(diff[2]), .Cout(_2_2_cout));
  xor xor_4 (xor_4_out, B[3], K);
  _1bit_full_adder _2_3 (.A(A[3]), .B(xor_4_out), .Cin(_2_2_cout), .Sum(diff[3]), .Cout(C));

  // Notes on the sheet:
  //   A: input bus
  //   B: input bus
endmodule
