// Digital circuit 4bit_full_adder.dig as structural Verilog
module _4bit_full_adder (
  input  [3:0] A,
  input  [3:0] B,
  input  Ci_1,
  output [3:0] Sum,
  output Overflow
);

  wire _2_0_cout, _2_1_cout, _2_2_cout;

  _1bit_full_adder _2_0 (.A(A[0]), .B(B[0]), .Cin(Ci_1), .Sum(Sum[0]), .Cout(_2_0_cout));
  _1bit_full_adder _2_1 (.A(A[1]), .B(B[1]), .Cin(_2_0_cout), .Sum(Sum[1]), .Cout(_2_1_cout));
  _1bit_full_adder _2_2 (.A(A[2]), .B(B[2]), .Cin(_2_1_cout), .Sum(Sum[2]), .Cout(_2_2_cout));
  _1bit_full_adder _2_3 (.A(A[3]), .B(B[3]), .Cin(_2_2_cout), .Sum(Sum[3]), .Cout(Overflow));
endmodule
